# Fritzing sketch hardware_layout_v0.1 (saved by Fritzing 0.9.3b)

parts:
  Raspberry_Pi_1 = Raspberry Pi 3 [part_number=RPI-3-V1.2]
  Test_Switch = Taiway 100-SP-X-T1 SPDT Miniature Toggle Switch [part_number=100-SP-X-T1-0-0-B1-M1 package=THT]
  DryContact1 = BANANA_CONN [package=banana_conn]
  DryContact2 = BANANA_CONN [package=banana_conn]

nets:
  N1: Raspberry_Pi_1.GIPO27, Test_Switch.L1
  N2: Raspberry_Pi_1.GIPO19, DryContact1.1
  N3: Raspberry_Pi_1.GND, Test_Switch.L2, DryContact2.1
